// Logisim project Final Project Combinational Circuit.circ as structural Verilog: 1 circuit, main circuit main
module main (
  input  A,
  input  [1:0] BC,
  output out_3,
  output out_4,
  output out_5,
  output out_6,
  output f,
  output a_2,
  output g,
  output b,
  output out_11,
  output c,
  output e,
  output d
);

  wire not_1_out;

  not not_1 (not_1_out, A);
  Decoder #(.select(2)) decoder_1 (.out0(out_3), .out1(out_4), .out2(out_5), .out3(out_6), .sel(BC), .en(1'b1));
  Multiplexer #(.select(2)) multiplexer_1 (
    .in0(A), .in1(1'b0), .in2(not_1_out), .in3(not_1_out), .out(a_2), .sel(BC), .en(1'b1));
  Multiplexer #(.select(2)) multiplexer_2 (
    .in0(A), .in1(not_1_out), .in2(not_1_out), .in3(1'b0), .out(b), .sel(BC), .en(1'b1));
  Multiplexer #(.select(2)) multiplexer_3 (
    .in0(1'b0), .in1(1'b1), .in2(1'b1), .in3(1'b0), .out(d), .sel(BC), .en(1'b1));
  nand nand_1 (e, out_6, A);
  _7_Segment_Display u_7_segment_display_1 (.g(a_2), .f(e), .a(a_2), .b(b), .e(e), .d(d), .c(b), .dp(e));

  assign c = b;
  assign f = e;
  assign g = a_2;
  assign out_11 = e;

  // Notes on the sheet:
  //   GND
  //   Vcc
endmodule
