// Logisim project Final Project Sequential Circuit.circ as structural Verilog: 1 circuit, main circuit main
module main (
  output f,
  output a,
  output g,
  output e,
  output c,
  output b,
  output d
);

  wire clock_1_out, j_k_ff_1_q, j_k_ff_1_qn, j_k_ff_2_qn, j_k_ff_3_qn, not_1_out, or_1_out, or_2_out,
       or_3_out, or_4_out;
  wire [1:0] j_k_ff_3_q;

  Clock clock_1 (.out(clock_1_out));
  J_K_Flip_Flop j_k_ff_1 (
    .J(or_1_out), .clk(clock_1_out), .K(or_1_out), .Q(j_k_ff_1_q), .Qn(j_k_ff_1_qn));  // open: preset, en, reset
  or or_1 (or_1_out, j_k_ff_3_qn, j_k_ff_3_q[1]);
  or or_2 (or_2_out, j_k_ff_1_qn, j_k_ff_3_q[0]);
  J_K_Flip_Flop j_k_ff_2 (
    .J(or_2_out), .clk(clock_1_out), .K(or_2_out), .Q(j_k_ff_3_q[1]), .Qn(j_k_ff_2_qn));  // open: preset, en, reset
  or or_3 (or_3_out, j_k_ff_2_qn, j_k_ff_1_qn);
  or or_4 (or_4_out, j_k_ff_3_q[1], j_k_ff_1_qn);
  J_K_Flip_Flop j_k_ff_3 (
    .J(or_4_out), .clk(clock_1_out), .K(or_3_out), .Q(j_k_ff_3_q[0]), .Qn(j_k_ff_3_qn));  // open: preset, en, reset
  not not_1 (not_1_out, j_k_ff_1_q);
  Multiplexer #(.select(2)) multiplexer_1 (
    .in0(j_k_ff_1_q), .in1(1'b0), .in2(not_1_out), .in3(not_1_out), .out(a), .sel(j_k_ff_3_q), .en(1'b1));
  Multiplexer #(.select(2)) multiplexer_2 (
    .in0(j_k_ff_1_q), .in1(not_1_out), .in2(not_1_out), .in3(1'b0), .out(b), .sel(j_k_ff_3_q), .en(1'b1));
  Multiplexer #(.select(2)) multiplexer_3 (
    .in0(1'b0), .in1(1'b1), .in2(1'b1), .in3(1'b0), .out(d), .sel(j_k_ff_3_q), .en(1'b1));
  nand nand_1 (e, j_k_ff_1_q, j_k_ff_3_q[1], j_k_ff_3_q[0]);
  _7_Segment_Display u_7_segment_display_1 (.g(a), .f(e), .a(a), .b(b), .e(e), .d(d), .c(b), .dp(e));

  assign c = b;
  assign f = e;
  assign g = a;

  // Notes on the sheet:
  //   A
  //   B
  //   C
  //   GND
  //   Vcc
endmodule
