// Logisim project Sequential IUBFALL.circ as structural Verilog: 1 circuit, main circuit main
module main (
  input  in_1,
  output out_2,
  output out_3,
  output out_4,
  output out_5,
  output f,
  output a,
  output g,
  output b,
  output out_10,
  output c,
  output e,
  output d
);

  wire and_1_out, clock_1_out, j_k_ff_3_q, not_1_out;
  wire [1:0] j_k_ff_1_q;

  Clock clock_1 (.out(clock_1_out));
  not not_1 (not_1_out, j_k_ff_3_q);
  J_K_Flip_Flop j_k_ff_1 (.J(in_1), .clk(clock_1_out), .K(in_1), .Q(j_k_ff_1_q[0]));  // open: Qn, preset, en, reset
  J_K_Flip_Flop j_k_ff_2 (
    .J(j_k_ff_1_q[0]), .clk(clock_1_out), .K(j_k_ff_1_q[0]), .Q(j_k_ff_1_q[1]));  // open: Qn, preset, en, reset
  and and_1 (and_1_out, j_k_ff_1_q[1], j_k_ff_1_q[0]);
  J_K_Flip_Flop j_k_ff_3 (
    .J(and_1_out), .clk(clock_1_out), .K(and_1_out), .Q(j_k_ff_3_q));  // open: Qn, preset, en, reset
  Decoder #(.select(2)) decoder_1 (.out0(out_2), .out1(out_3), .out2(out_4), .out3(out_5), .sel(j_k_ff_1_q), .en(1'b1));
  Multiplexer #(.select(2)) multiplexer_1 (
    .in0(j_k_ff_3_q), .in1(1'b0), .in2(not_1_out), .in3(not_1_out), .out(a), .sel(j_k_ff_1_q), .en(1'b1));
  Multiplexer #(.select(2)) multiplexer_2 (
    .in0(j_k_ff_3_q), .in1(not_1_out), .in2(not_1_out), .in3(1'b0), .out(b), .sel(j_k_ff_1_q), .en(1'b1));
  Multiplexer #(.select(2)) multiplexer_3 (
    .in0(1'b0), .in1(1'b1), .in2(1'b1), .in3(1'b0), .out(d), .sel(j_k_ff_1_q), .en(1'b1));
  nand nand_1 (e, out_5, j_k_ff_3_q);
  _7_Segment_Display u_7_segment_display_1 (.g(a), .f(e), .a(a), .b(b), .e(e), .d(d), .c(b), .dp(e));

  assign c = b;
  assign f = e;
  assign g = a;
  assign out_10 = e;

  // Notes on the sheet:
  //   GND
  //   Vcc
endmodule
